// Logisim project alu.circ as structural Verilog: 12 circuits, main circuit main
module main (
  input  [31:0] X,
  input  [31:0] Y,
  input  [5:0] Switch__S,
  output Signed_Overflow,
  output [31:0] RESULT,
  output Equal
);

  wire add_overflow, sub_overflow;
  wire [31:0] add_out, addu_out, and_out, bitpal_out, lfsr_out, or_out, sll_out, slt_out, sltu_out, sra_out,
       srl_out, sub_out, subu_out;

  sll sll_1 (.inp1(X), .inp2(Y), .out(sll_out));
  srl srl_1 (.inp1(X), .inp2(Y), .out(srl_out));
  sra sra_1 (.inp1(X), .inp2(Y), .out(sra_out));
  assign and_out = X & Y;  // AND_Gate and, 32 bits wide
  assign or_out = X | Y;  // OR_Gate or, 32 bits wide
  add add_1 (.inp1(X), .inp2(Y), .overflow(add_overflow), .out(add_out));
  addu addu_1 (.inp1(X), .inp2(Y), .out(addu_out));
  sub sub_1 (.inp1(X), .inp2(Y), .overflow(sub_overflow), .out(sub_out));
  subu subu_1 (.inp1(X), .inp2(Y), .out(subu_out));
  slt slt_1 (.inp1(X), .inp2(Y), .out(slt_out));
  sltu sltu_1 (.inp1(X), .inp2(Y), .out(sltu_out));
  lfsr lfsr_1 (.\input (X), .out(lfsr_out));
  bitpal bitpal_1 (.\input (X), .out(bitpal_out));

  // Notes on the sheet:
  //   INPUTS to your circuit
  //   INPUT to your circuit
  //   DON'T CHANGE THE INPUTS AND OUTPUTS! IF YOU DO SO, YOU NEED TO MAKE SURE THE PINS ARE IN THE RIGHT PLACES!
  //   OUTPUTS of your circuit
endmodule

module sll (
  input  [31:0] inp1,
  input  [31:0] inp2,
  output [31:0] out
);

  wire [4:0] bit_extender_1_out;

  Bit_Extender #(.in_width(32), .out_width(5)) bit_extender_1 (.in(inp2), .out(bit_extender_1_out));
  Shifter #(.width(32)) shifter_1 (.in(inp1), .\dist (bit_extender_1_out), .out(out));
endmodule

module srl (
  input  [31:0] inp1,
  input  [31:0] inp2,
  output [31:0] out
);

  wire [4:0] bit_extender_1_out;

  Bit_Extender #(.in_width(32), .out_width(5)) bit_extender_1 (.in(inp2), .out(bit_extender_1_out));
  Shifter #(.width(32), .shift("lr")) shifter_1 (.in(inp1), .\dist (bit_extender_1_out), .out(out));
endmodule

module sra (
  input  [31:0] inp1,
  input  [31:0] inp2,
  output [31:0] out
);

  wire [4:0] bit_extender_1_out;

  Bit_Extender #(.in_width(32), .out_width(5)) bit_extender_1 (.in(inp2), .out(bit_extender_1_out));
  Shifter #(.width(32), .shift("ar")) shifter_1 (.in(inp1), .\dist (bit_extender_1_out), .out(out));
endmodule

module add (
  input  [31:0] inp1,
  input  [31:0] inp2,
  output [31:0] out,
  output overflow
);

  Adder #(.width(32)) adder_1 (.a(inp1), .b(inp2), .out(out), .cout(overflow));  // open: cin
endmodule

module addu (
  input  [31:0] inp1,
  input  [31:0] inp2,
  output [31:0] out
);

  Adder #(.width(32)) adder_1 (.a(inp1), .b(inp2), .out(out));  // open: cin, cout
endmodule

module sub (
  input  [31:0] inp1,
  input  [31:0] inp2,
  output [31:0] out,
  output overflow
);

  Subtractor #(.width(32)) subtractor_1 (.a(inp1), .b(inp2), .out(out), .bout(overflow));  // open: bin
endmodule

module subu (
  input  [31:0] inp1,
  input  [31:0] inp2,
  output [31:0] out
);

  Subtractor #(.width(32)) subtractor_1 (.a(inp1), .b(inp2), .out(out));  // open: bin, bout
endmodule

module slt (
  input  [31:0] inp1,
  input  [31:0] inp2,
  output [31:0] out
);

  wire comparator_1_lt;

  Comparator #(.width(32)) comparator_1 (.a(inp1), .b(inp2), .lt(comparator_1_lt));  // open: gt, eq
  assign out = {{31{1'b0}}, comparator_1_lt};  // Bit_Extender bit_extender_1
endmodule

module sltu (
  input  [31:0] inp1,
  input  [31:0] inp2,
  output [31:0] out
);

  wire comparator_1_lt;

  Comparator #(.width(32), .mode("unsigned")) comparator_1 (.a(inp1), .b(inp2), .lt(comparator_1_lt));  // open: gt, eq
  assign out = {{31{1'b0}}, comparator_1_lt};  // Bit_Extender bit_extender_1
endmodule

module bitpal (
  input  [31:0] \input ,
  output [31:0] out
);

  wire comparator_1_eq;

  Comparator #(.width(16)) comparator_1 (
    .a(\input [15:0]),
    .b({\input [16], \input [17], \input [18], \input [19], \input [20], \input [21], \input [22], \input [23], \input [24], \input [25], \input [26], \input [27], \input [28], \input [29], \input [30], \input [31]}),
    .eq(comparator_1_eq));  // open: gt, lt
  assign out = {{31{1'b0}}, comparator_1_eq};  // Bit_Extender bit_extender_1
endmodule

module lfsr (
  input  [31:0] \input ,
  output [31:0] out
);

  wire xor_1_out, xor_2_out;

  xor xor_1 (xor_1_out, \input [0], \input [2]);
  xor xor_2 (xor_2_out, xor_1_out, \input [3]);
  xor xor_3 (out[31], xor_2_out, \input [5]);

  assign out[30:0] = \input [31:1];

  // Other names for the same wires on the sheet: _0 = \input [0]; inp[31:0] = \input ; _2 = \input [2];
  //   _3 = \input [3]; _5 = \input [5]
endmodule
