// Logisim project cpu.circ as structural Verilog: 4 circuits, main circuit main
module main (
  input  [31:0] RS_READ_VALUE,
  input  [31:0] RT_READ_VALUE,
  input  [31:0] INSTRUCTION,
  input  CLOCK,
  input  RESET,
  output [31:0] t0,
  output [31:0] t1,
  output [31:0] t2,
  output [31:0] t3,
  output [4:0] RS,
  output [4:0] RT,
  output [4:0] Write_Register,
  output [31:0] RD_WRITE_VALUE,
  output RD_WRITE_ENABLE,
  output [23:0] FETCH_ADDRESS
);

  wire ALUSrc, check_if_t0_t3_1_if_t0_t3, check_if_t0_t3_2_if_t0_t3, check_if_t0_t3_3_if_t0_t3, RegDst,
       write_regfile, WriteReg;
  wire [31:0] imm, multiplexer_2_out, multiplexer_3_out, multiplexer_4_out, regfile_wrapper_1_read_data_1,
       regfile_wrapper_1_read_data_2;

  not not_1 (RD_WRITE_ENABLE, write_regfile);
  cpu_control cpu_control_1 ();  // open: opcode, funct, RegDst, ALUSrc, shift, lui, ALUCtr, access_byte, MemToReg, MemWrite, beq, bne, jump, RegWrite, ExtOp
  assign imm = {{16{INSTRUCTION[15]}}, INSTRUCTION[15:0]};  // Bit_Extender bit_extender_1
  Multiplexer #(.width(5)) multiplexer_1 (
    .in0(INSTRUCTION[20:16]), .in1(INSTRUCTION[15:11]), .out(Write_Register), .sel(RegDst));  // open: en
  check_if_t0_t3 check_if_t0_t3_1 (.\reg (Write_Register), .if_t0_t3(check_if_t0_t3_1_if_t0_t3));
  and and_1 (write_regfile, check_if_t0_t3_1_if_t0_t3, WriteReg);
  // regfile_main RegFile: pin names not known
  // mem_main MEM: pin names not known
  check_if_t0_t3 check_if_t0_t3_2 (.\reg (INSTRUCTION[25:21]), .if_t0_t3(check_if_t0_t3_2_if_t0_t3));
  regfile_wrapper regfile_wrapper_1 (
    .read_register_1(INSTRUCTION[25:21]), .read_register_2(INSTRUCTION[20:16]),
    .write_register(Write_Register), .t0(t0), .t1(t1), .t2(t2), .t3(t3), .RegWrite(write_regfile),
    .clock(CLOCK), .read_data_1(regfile_wrapper_1_read_data_1), .read_data_2(regfile_wrapper_1_read_data_2));  // open: write_data
  check_if_t0_t3 check_if_t0_t3_3 (.\reg (INSTRUCTION[20:16]), .if_t0_t3(check_if_t0_t3_3_if_t0_t3));
  Multiplexer #(.width(32)) multiplexer_2 (
    .in0(RS_READ_VALUE), .in1(regfile_wrapper_1_read_data_1), .out(multiplexer_2_out),
    .sel(check_if_t0_t3_2_if_t0_t3));  // open: en
  Multiplexer #(.width(32)) multiplexer_3 (
    .in0(RT_READ_VALUE), .in1(regfile_wrapper_1_read_data_2), .out(multiplexer_3_out),
    .sel(check_if_t0_t3_3_if_t0_t3));  // open: en
  Multiplexer #(.width(32)) multiplexer_4 (
    .in0(multiplexer_3_out), .in1(imm), .out(multiplexer_4_out), .sel(ALUSrc));  // open: en
  alu_main ALU (.X(multiplexer_2_out), .Y(multiplexer_4_out));  // open: Switch__S, Equal, RESULT, Signed_Overflow

  assign RS = INSTRUCTION[25:21];
  assign RT = INSTRUCTION[20:16];

  // Other names for the same wires on the sheet: clk = CLOCK; rd[4:0] = INSTRUCTION[15:11];
  //   opcode[5:0] = INSTRUCTION[31:26]; rt_rd[4:0] = Write_Register; run_rs_val[31:0] = RS_READ_VALUE;
  //   run_rt_val[31:0] = RT_READ_VALUE

  // Notes on the sheet:
  //   These are outputs/inputs from run.circ
  //   These are outputs to run.circ
  //   Feel free to move these components
endmodule

module check_if_t0_t3 (
  input  [4:0] \reg ,
  output if_t0_t3
);

  wire comparator_1_lt, comparator_2_gt;

  Comparator #(.width(5), .mode("unsigned")) comparator_1 (
    .a(\reg ), .b(5'b01100), .lt(comparator_1_lt));  // open: gt, eq
  Comparator #(.width(5), .mode("unsigned")) comparator_2 (
    .a(\reg ), .b(5'b00111), .gt(comparator_2_gt));  // open: eq, lt
  and \and  (if_t0_t3, comparator_1_lt, comparator_2_gt);
endmodule

module cpu_control (
  input  [5:0] opcode,
  input  [5:0] funct,
  output RegDst,
  output ALUSrc,
  output shift,
  output lui,
  output [5:0] ALUCtr,
  output access_byte,
  output MemToReg,
  output MemWrite,
  output beq,
  output bne,
  output jump,
  output RegWrite,
  output ExtOp
);

  wire addiu, and_1_out, and_2_out, andi, comparator_14_eq, comparator_15_eq, comparator_16_eq, j, jal, jr,
       lb, lbu, lw, not_2_out, or_4_out, or_5_out, or_6_out, or_7_out, ori;

  and and_1 (and_1_out, RegDst, jr);
  Comparator #(.width(6), .mode("unsigned")) comparator_1 (.a({6{1'b0}}), .b(opcode), .eq(RegDst));  // open: gt, lt
  Comparator #(.width(6), .mode("unsigned")) comparator_2 (.a(6'b001001), .b(opcode), .eq(addiu));  // open: gt, lt
  Comparator #(.width(6), .mode("unsigned")) comparator_3 (.a(6'b001100), .b(opcode), .eq(andi));  // open: gt, lt
  Comparator #(.width(6), .mode("unsigned")) comparator_4 (.a(6'b001101), .b(opcode), .eq(ori));  // open: gt, lt
  Comparator #(.width(6), .mode("unsigned")) comparator_5 (.a(6'b001111), .b(opcode), .eq(lui));  // open: gt, lt
  Comparator #(.width(6), .mode("unsigned")) comparator_6 (.a(6'b100000), .b(opcode), .eq(lb));  // open: gt, lt
  Comparator #(.width(6), .mode("unsigned")) comparator_7 (.a(6'b100100), .b(opcode), .eq(lbu));  // open: gt, lt
  Comparator #(.width(6), .mode("unsigned")) comparator_8 (.a(6'b100011), .b(opcode), .eq(lw));  // open: gt, lt
  Comparator #(.width(6), .mode("unsigned")) comparator_9 (.a(6'b101011), .b(opcode), .eq(MemWrite));  // open: gt, lt
  Comparator #(.width(6), .mode("unsigned")) comparator_10 (.a(6'b000100), .b(opcode), .eq(beq));  // open: gt, lt
  Comparator #(.width(6), .mode("unsigned")) comparator_11 (.a(6'b000101), .b(opcode), .eq(bne));  // open: gt, lt
  Comparator #(.width(6), .mode("unsigned")) comparator_12 (.a(6'b000010), .b(opcode), .eq(j));  // open: gt, lt
  Comparator #(.width(6), .mode("unsigned")) comparator_13 (.a(6'b000011), .b(opcode), .eq(jal));  // open: gt, lt
  nor nor_1 (RegWrite, and_1_out, j, jal, MemWrite, beq, bne);
  nor nor_2 (ExtOp, andi, ori);
  not not_1 (ALUSrc, RegDst);
  or or_1 (access_byte, lb, lbu);
  or or_2 (MemToReg, lb, lbu, lw);
  or or_3 (jump, j, jal);
  not not_2 (not_2_out, jr);
  assign ALUCtr = and_2_out ? funct : 6'bz;  // Controlled_Buffer controlled_buffer_1
  and and_2 (and_2_out, RegDst, not_2_out);
  assign ALUCtr = or_4_out ? 6'b100001 : 6'bz;  // Controlled_Buffer controlled_buffer_2
  or or_4 (or_4_out, lb, lbu, lw, MemWrite, addiu);
  assign ALUCtr = andi ? 6'b100100 : 6'bz;  // Controlled_Buffer controlled_buffer_3
  assign ALUCtr = or_5_out ? 6'b100101 : 6'bz;  // Controlled_Buffer controlled_buffer_4
  or or_5 (or_5_out, ori, j, jal);
  assign ALUCtr = or_6_out ? 6'b100011 : 6'bz;  // Controlled_Buffer controlled_buffer_5
  or or_6 (or_6_out, j, bne);
  Comparator #(.width(6), .mode("unsigned")) comparator_14 (
    .a({6{1'b0}}), .b(funct), .eq(comparator_14_eq));  // open: gt, lt
  Comparator #(.width(6), .mode("unsigned")) comparator_15 (
    .a(6'b000010), .b(funct), .eq(comparator_15_eq));  // open: gt, lt
  Comparator #(.width(6), .mode("unsigned")) comparator_16 (
    .a(6'b000011), .b(funct), .eq(comparator_16_eq));  // open: gt, lt
  Comparator #(.width(6), .mode("unsigned")) comparator_17 (.a(6'b001000), .b(funct), .eq(jr));  // open: gt, lt
  and and_3 (shift, RegDst, or_7_out);
  or or_7 (or_7_out, comparator_14_eq, comparator_15_eq, comparator_16_eq);

  // Other names for the same wires on the sheet: R = RegDst; sw = MemWrite
endmodule

module regfile_wrapper (
  input  [4:0] read_register_1,
  input  [4:0] read_register_2,
  input  [4:0] write_register,
  input  RegWrite,
  input  clock,
  input  [31:0] write_data,
  output [31:0] t0,
  output [31:0] t1,
  output [31:0] t2,
  output [31:0] t3,
  output [31:0] read_data_1,
  output [31:0] read_data_2
);

  wire [1:0] bit_extender_1_out, bit_extender_2_out, bit_extender_3_out;

  Bit_Extender #(.in_width(5), .out_width(2)) bit_extender_1 (.in(read_register_1), .out(bit_extender_1_out));
  Bit_Extender #(.in_width(5), .out_width(2)) bit_extender_2 (.in(read_register_2), .out(bit_extender_2_out));
  Bit_Extender #(.in_width(5), .out_width(2)) bit_extender_3 (.in(write_register), .out(bit_extender_3_out));
  regfile_main regfile (
    .Read_register_1(bit_extender_1_out), .Read_register_2(bit_extender_2_out),
    .write_register(bit_extender_3_out), .write_data(write_data), .t0_Value(t0), .t1_Value(t1),
    .t2_Value(t2), .t3_Value(t3), .RegWrite(RegWrite), .clock(clock), .Read_Data_1(read_data_1),
    .Read_Data_2(read_data_2));

  // Notes on the sheet:
  //   regfile wrapper whose register inputs are 5 bits rather than 2 bits
endmodule
